# Fritzing sketch Arduino nano Version (saved by Fritzing 0.9.6b)

parts:
  HC-SR04_Sensor_1 = HC-SR04 Ultrasonic Distance Sensor
  S1 = Pololu QTR-8 Reflectabce Sensor array [package=THT]
  M1 = DC Motor
  M2 = DC Motor
  U2 = LIPO-110mAh [package=lipo-110]
  U3 = LIPO-110mAh [package=lipo-110]
  U4 = LIPO-110mAh [package=lipo-110]
  U5 = SWITCH_SPDT [package=kps-1290]
  S2 = Pololu DRV 8833 Dual Motor Driver Carrier [part_number=DRV8833]
  S2_1 = Pololu DRV 8833 Dual Motor Driver Carrier [part_number=DRV8833]  # not connected
  S2_2 = Pololu DRV 8833 Dual Motor Driver Carrier [part_number=DRV8833]  # not connected
  Part1 = Arduino Nano (Rev3.0)

nets:
  VCC: HC-SR04_Sensor_1.VCC, S1.pin2, S1.pin14, Part1.5V
  N1: HC-SR04_Sensor_1.TRIG, Part1.D8
  N2: HC-SR04_Sensor_1.ECHO, Part1.D7
  GND: HC-SR04_Sensor_1.GND, S1.pin1, S1.pin15, Part1.GND
  N3: S1.pin5, Part1.A7
  N4: S1.pin6, Part1.A6
  N5: S1.pin7, Part1.A5
  N6: S1.pin8, Part1.A4
  N7: S1.pin9, Part1.A3
  N8: S1.pin10, Part1.A2
  N9: S1.pin11, Part1.A1
  N10: S1.pin12, Part1.A0
  N11: M1.pin_1, S2.AOUT2
  N12: M1.pin_2, S2.AOUT1
  N13: M2.pin_1, S2.BOUT1
  N14: M2.pin_2, S2.BOUT2
  N15: U2.+, U5.O
  N16: U2.-, U3.+
  N17: U3.-, U4.+
  N18: U5.S, S2.connector2
  N19: S2.connector1, S2.GND
  N20: S2.connector3, Part1.D6
  N21: S2.connector4, Part1.D3
  N22: S2.connector5, Part1.D4
  N23: S2.connector6, Part1.D5
